// Logisim project counter.circ as structural Verilog: 8 circuits, main circuit main
module main (
  output A0,
  output A1,
  output A2,
  output A3
);

  wire and_1_out, CLK_out;

  Clock CLK (.out(CLK_out));
  TRTrigger trtrigger_1 (.T(CLK_out), .RST(and_1_out), .Q(A0));
  TRTrigger trtrigger_2 (.T(A0), .RST(and_1_out), .Q(A1));
  TRTrigger trtrigger_3 (.T(A1), .RST(and_1_out), .Q(A2));
  TRTrigger trtrigger_4 (.T(A2), .RST(and_1_out), .Q(A3));
  and and_1 (and_1_out, A3, A2, A0);
endmodule

module RSTrigger (
  input  R,
  input  S,
  output Q,
  output nQ
);

  wire or_1_out, por_1_out;

  POR #(.PorHighDuration(1)) por_1 (.out(por_1_out));
  or or_1 (or_1_out, por_1_out, R);
  nor nor_1 (Q, or_1_out, nQ);
  nor nor_2 (nQ, Q, S);
endmodule

module SRSTrigger (
  input  R,
  input  C,
  input  S,
  output Q,
  output nQ
);

  wire and_1_out, and_2_out;

  and and_1 (and_1_out, R, C);
  and and_2 (and_2_out, C, S);
  RSTrigger rstrigger_1 (.R(and_1_out), .S(and_2_out), .Q(Q), .nQ(nQ));
endmodule

module SRSRTrigger (
  input  R,
  input  C,
  input  S,
  input  RST,
  output Q,
  output nQ
);

  wire and_1_out, and_2_out, or_1_out;

  and and_1 (and_1_out, R, C);
  and and_2 (and_2_out, C, S);
  or or_1 (or_1_out, and_1_out, RST);
  RSTrigger rstrigger_1 (.R(or_1_out), .S(and_2_out), .Q(Q), .nQ(nQ));
endmodule

module JKTrigger (
  input  K,
  input  C,
  input  J,
  output Q,
  output NQ
);

  wire and_1_out, and_2_out, not_1_out, srstrigger_1_nq, srstrigger_1_q;

  and and_1 (and_1_out, Q, K);
  and and_2 (and_2_out, J, NQ);
  SRSTrigger srstrigger_1 (.R(and_1_out), .C(C), .S(and_2_out), .Q(srstrigger_1_q), .nQ(srstrigger_1_nq));
  not not_1 (not_1_out, C);
  SRSTrigger srstrigger_2 (.R(srstrigger_1_nq), .C(not_1_out), .S(srstrigger_1_q), .Q(Q), .nQ(NQ));
endmodule

module JKRTrigger (
  input  K,
  input  C,
  input  J,
  input  RST,
  output Q,
  output nQ
);

  wire and_1_out, and_2_out, not_1_out, srsrtrigger_1_nq, srsrtrigger_1_q;

  and and_1 (and_1_out, Q, K);
  and and_2 (and_2_out, J, nQ);
  SRSRTrigger srsrtrigger_1 (
    .R(and_1_out), .C(C), .S(and_2_out), .RST(RST), .Q(srsrtrigger_1_q), .nQ(srsrtrigger_1_nq));
  not not_1 (not_1_out, C);
  SRSRTrigger srsrtrigger_2 (.R(srsrtrigger_1_nq), .C(not_1_out), .S(srsrtrigger_1_q), .RST(RST), .Q(Q), .nQ(nQ));
endmodule

module DTrigger (
  input  D,
  input  C,
  output Q,
  output nQ
);

  wire not_1_out;

  not not_1 (not_1_out, D);
  SRSTrigger srstrigger_1 (.R(D), .C(C), .S(not_1_out), .Q(Q), .nQ(nQ));
endmodule

module TRTrigger (
  input  T,
  input  RST,
  output Q
);

  wire nand_1_out;

  nand nand_1 (nand_1_out, 1'b1, RST);
  JKRTrigger jkrtrigger_1 (.K(1'b1), .C(T), .J(nand_1_out), .RST(RST), .Q(Q));  // open: nQ
endmodule
