// Logisim project lfsr.circ as structural Verilog: 5 circuits, main circuit main
module main (
  output A0,
  output A1,
  output A2,
  output A3,
  output A4,
  output A5,
  output A6,
  output A7,
  output A8,
  output A9,
  output A10
);

  wire CLK_out, or_1_out, or_2_out, por_1_out, xor_1_out, xor_2_out;

  Clock CLK (.out(CLK_out));
  POR por_1 (.out(por_1_out));
  or or_1 (or_1_out, xor_1_out, por_1_out);
  or or_2 (or_2_out, por_1_out, CLK_out);
  DTrigger DTR0 (.D(or_1_out), .C(or_2_out), .Q(A0));
  DTrigger DTR5 (.D(A4), .C(CLK_out), .Q(A5));
  xor xor_1 (xor_1_out, A0, xor_2_out);
  DTrigger DTR1 (.D(A0), .C(CLK_out), .Q(A1));
  DTrigger DTR6 (.D(A5), .C(CLK_out), .Q(A6));
  DTrigger DTR2 (.D(A1), .C(CLK_out), .Q(A2));
  DTrigger DTR7 (.D(A6), .C(CLK_out), .Q(A7));
  xor xor_2 (xor_2_out, A7, A10);
  DTrigger DTR3 (.D(A2), .C(CLK_out), .Q(A3));
  DTrigger DTR8 (.D(A7), .C(CLK_out), .Q(A8));
  DTrigger DTR4 (.D(A3), .C(CLK_out), .Q(A4));
  DTrigger DTR9 (.D(A8), .C(CLK_out), .Q(A9));
  DTrigger DTR10 (.D(A9), .C(CLK_out), .Q(A10));
endmodule

module RSTrigger (
  input  R,
  input  S,
  output Q,
  output nQ
);

  wire or_1_out, por_1_out;

  POR #(.PorHighDuration(1)) por_1 (.out(por_1_out));
  or or_1 (or_1_out, por_1_out, R);
  nor nor_1 (Q, or_1_out, nQ);
  nor nor_2 (nQ, Q, S);
endmodule

module SRSTrigger (
  input  S,
  input  C,
  input  R,
  output Q,
  output nQ
);

  wire and_1_out, and_2_out;

  and and_1 (and_1_out, S, C);
  and and_2 (and_2_out, C, R);
  RSTrigger rstrigger_1 (.R(and_1_out), .S(and_2_out), .Q(Q), .nQ(nQ));
endmodule

module JKTrigger (
  input  K,
  input  C,
  input  J,
  output Q,
  output nQ
);

  wire and_1_out, and_2_out, not_1_out, srstrigger_1_nq, srstrigger_1_q;

  and and_1 (and_1_out, Q, K);
  and and_2 (and_2_out, J, nQ);
  SRSTrigger srstrigger_1 (.S(and_1_out), .C(C), .R(and_2_out), .Q(srstrigger_1_q), .nQ(srstrigger_1_nq));
  not not_1 (not_1_out, C);
  SRSTrigger srstrigger_2 (.S(srstrigger_1_nq), .C(not_1_out), .R(srstrigger_1_q), .Q(Q), .nQ(nQ));
endmodule

module DTrigger (
  input  D,
  input  C,
  output Q
);

  wire not_1_out;

  not not_1 (not_1_out, D);
  JKTrigger jktrigger_1 (.K(not_1_out), .C(C), .J(D), .Q(Q));  // open: nQ
endmodule
